# Fritzing sketch circuit (saved by Fritzing 0.9.3b)
breadboards: 1

parts:
  R1 = Resistor [tolerance=±5% resistance=220 package=THT]
  R2 = Resistor [tolerance=±5% resistance=220 package=THT]
  R3 = Resistor [tolerance=±5% resistance=220 package=THT]
  S1 = Pushbutton [package="[THT]"]
  LED1 = LED - 5mm [color="Red (633nm)" package="5 mm [THT]"]
  LED2 = LED - 5mm [color="Red (633nm)" package="5 mm [THT]"]
  LED3 = LED - 5mm [color="Red (633nm)" package="5 mm [THT]"]
  Bauteil1 = Arduino Nano (Rev3.0)

nets:
  N1: R1.Pin_0, LED1.anode
  N2: R1.Pin_1, Bauteil1.D3
  N3: R2.Pin_0, LED2.anode
  N4: R2.Pin_1, Bauteil1.D4
  N5: R3.Pin_0, LED3.anode
  N6: R3.Pin_1, Bauteil1.D5
  N7: S1.Pin_1, S1.Pin_2
  N8: S1.Pin_3, S1.Pin_4, LED1.cathode, LED2.cathode, LED3.cathode, Bauteil1.GND

notes:
  wire color equals led color
